# Fritzing sketch main (saved by Fritzing 0.8.3b)
breadboards: 1

parts:
  Raspberry_Pi_rev1 = Raspberry Pi rev2
  DS1 = DS18B20 1-Wire Temperature Sensor [part_number=DS18B20]
  GPS1 = Adafruit Ultimate GPS Breakout
  Pi1 = Adafruit Pi Cobbler
  LED1 = RGB LED (com. anode, rbg) [package="5 mm [THT]"]  # not connected
  CAMERA1 = TTL Serial JPEG Camera
  F1 = FUSE [package=fuse_5mm]
  J3 = Power Jack [package=power_jack_smd]
  U1 = Voltage Regulator [package=to220-adj]
  R1 = Resistor [tolerance=±5% resistance=220 package="1206 [SMD]"]

nets:
  3V3: Raspberry_Pi_rev1.3V3, DS1.VDD, GPS1.3.3V, GPS1.EN, GPS1.VBAT, GPS1.FIX, Pi1.3V3
  GND: Raspberry_Pi_rev1.GND, GPS1.GND, GPS1.VIN, GPS1.PPS, Pi1.GND
  N1: Raspberry_Pi_rev1.GPIO_23, Pi1.#4, R1.Pin_0
  N2: Raspberry_Pi_rev1.GPIO_14, Raspberry_Pi_rev1.GPIO_15, Raspberry_Pi_rev1.GPIO4, Pi1.TXD, Pi1.RXD, Pi1.#18, Pi1.PIN14, Pi1.#23
  N3: Raspberry_Pi_rev1.GPIO_24, Pi1.#24
  N4: Raspberry_Pi_rev1.GPIO_25, Pi1.#25, Pi1.CE0, Pi1.CE1
  N5: DS1.DQ, R1.Pin_1
  N6: CAMERA1.CVBS, CAMERA1.GND, CAMERA1.TX, CAMERA1.RX
  N7: F1.1, J3.GNDBREAK
  N8: F1.2, U1.IN
  N9: J3.GND, U1.ADJ

notes:
  Pi Camera connected
  using CSi interface
  1A
  INPUT: 12-17V
  OUTPUT: 5V

custom parts:
  Adafruit Pi Cobbler: Adafruit Pi Cobbler GPIO Breakout for Raspberry Pi
  TTL Serial JPEG Camera: TTL Serial JPEG Camera with NTSC Out
